// Logisim project my-cpu.circ as structural Verilog: 10 circuits, main circuit full-cpu
module _1_bit_alu (
  input  LSin,
  input  CI,
  input  A,
  input  A_S,
  input  B,
  input  [2:0] Select,
  input  SLT,
  input  RSin,
  output FAout,
  output ALUout,
  output CO
);

  wire and_1_out, not_1_out, or_1_out, xor_1_out;

  and and_1 (and_1_out, A, B);
  or or_1 (or_1_out, A, B);
  Adder #(.width(1)) adder_1 (.a(A), .b(xor_1_out), .out(FAout), .cin(CI), .cout(CO));
  xor xor_1 (xor_1_out, A_S, B);
  not not_1 (not_1_out, A);
  Multiplexer #(.select(3), .width(1)) multiplexer_1 (
    .in0(and_1_out), .in1(or_1_out), .in2(FAout), .in3(SLT), .in4(not_1_out), .in5(LSin), .in6(RSin),
    .out(ALUout), .sel(Select));  // open: in7
endmodule

module _4_bit_alu (
  input  LSin,
  input  [3:0] A,
  input  [3:0] B,
  input  [2:0] Select,
  input  CI,
  input  Add_Sub,
  input  [3:0] SLT,
  input  RSin,
  output [3:0] Result,
  output overflow,
  output CO,
  output FAout
);

  wire n1_bit_alu_1_co, n1_bit_alu_2_co, n1_bit_alu_3_co;

  _1_bit_alu u_1_bit_alu_1 (
    .A(A[0]), .B(B[0]), .SLT(SLT[0]), .LSin(LSin), .A_S(Add_Sub), .CI(CI), .Select(Select), .RSin(A[1]),
    .CO(n1_bit_alu_1_co), .ALUout(Result[0]));  // open: FAout
  _1_bit_alu u_1_bit_alu_2 (
    .A(A[1]), .B(B[1]), .SLT(SLT[1]), .LSin(A[0]), .A_S(Add_Sub), .CI(n1_bit_alu_1_co), .Select(Select),
    .RSin(A[2]), .CO(n1_bit_alu_2_co), .ALUout(Result[1]));  // open: FAout
  _1_bit_alu u_1_bit_alu_3 (
    .A(A[2]), .B(B[2]), .SLT(SLT[2]), .LSin(A[1]), .A_S(Add_Sub), .CI(n1_bit_alu_2_co), .Select(Select),
    .RSin(A[3]), .CO(n1_bit_alu_3_co), .ALUout(Result[2]));  // open: FAout
  _1_bit_alu u_1_bit_alu_4 (
    .A(A[3]), .B(B[3]), .SLT(SLT[3]), .LSin(A[2]), .A_S(Add_Sub), .CI(n1_bit_alu_3_co), .Select(Select),
    .RSin(RSin), .CO(CO), .FAout(FAout), .ALUout(Result[3]));
  xor xor_1 (overflow, n1_bit_alu_3_co, CO);

  // Notes on the sheet:
  //   0
  //   1
  //   2
  //   3
endmodule

module _16_bit_alu (
  input  Add_Sub,
  input  [2:0] Select,
  input  [15:0] A,
  input  [15:0] B,
  output z_e_r_o,
  output [15:0] Result,
  output Overflow
);

  wire n4_bit_alu_1_co, n4_bit_alu_2_co, n4_bit_alu_3_co, nor_1_out, nor_2_out;
  wire [0:0] n4_bit_alu_4_faout;

  _4_bit_alu u_4_bit_alu_1 (
    .A(A[3:0]), .B(B[3:0]), .SLT({3'b000, n4_bit_alu_4_faout[0]}), .Add_Sub(Add_Sub), .LSin(1'b0),
    .CI(Add_Sub), .Select(Select), .RSin(A[4]), .CO(n4_bit_alu_1_co), .Result(Result[3:0]));  // open: FAout, overflow
  _4_bit_alu u_4_bit_alu_2 (
    .A(A[7:4]), .B(B[7:4]), .SLT(4'b0000), .Add_Sub(Add_Sub), .LSin(A[3]), .CI(n4_bit_alu_1_co),
    .Select(Select), .RSin(A[8]), .CO(n4_bit_alu_2_co), .Result(Result[7:4]));  // open: FAout, overflow
  _4_bit_alu u_4_bit_alu_3 (
    .A(A[11:8]), .B(B[11:8]), .SLT(4'b0000), .Add_Sub(Add_Sub), .LSin(A[7]), .CI(n4_bit_alu_2_co),
    .Select(Select), .RSin(A[12]), .CO(n4_bit_alu_3_co), .Result(Result[11:8]));  // open: FAout, overflow
  _4_bit_alu u_4_bit_alu_4 (
    .A(A[15:12]), .B(B[15:12]), .SLT(4'b0000), .Add_Sub(Add_Sub), .LSin(A[11]), .CI(n4_bit_alu_3_co),
    .Select(Select), .RSin(A[15]), .FAout(n4_bit_alu_4_faout[0]), .Result(Result[15:12]), .overflow(Overflow));  // open: CO
  nor nor_1 (nor_1_out, Result[0], Result[1], Result[2], Result[3], Result[4], Result[5], Result[6], Result[7], Result[8]);
  nor nor_2 (nor_2_out, Result[9], Result[10], Result[11], Result[12], Result[13], Result[14], Result[15]);
  and and_1 (z_e_r_o, nor_1_out, nor_2_out);

  // Notes on the sheet:
  //   0-3
  //   4-7
  //   8-11
  //   12-15
endmodule

module reg_file (
  input  [15:0] WriteData,
  input  [3:0] ReadAddress1,
  input  CLK,
  input  Write,
  input  [3:0] ReadAddress2,
  input  Clear,
  input  [3:0] ReadAddress3,
  input  [3:0] WriteAddress,
  output [15:0] Out1,
  output [15:0] Out2,
  output [15:0] Out3
);

  wire n4_to_16_decoder_w_enable_1__1, n4_to_16_decoder_w_enable_1__2, n4_to_16_decoder_w_enable_1__3,
       n4_to_16_decoder_w_enable_1__4, n4_to_16_decoder_w_enable_1__5, n4_to_16_decoder_w_enable_1__6,
       n4_to_16_decoder_w_enable_1__7, n4_to_16_decoder_w_enable_1__8, n4_to_16_decoder_w_enable_1__9,
       n4_to_16_decoder_w_enable_1__10, n4_to_16_decoder_w_enable_1__11, n4_to_16_decoder_w_enable_1__12,
       n4_to_16_decoder_w_enable_1__13, n4_to_16_decoder_w_enable_1__14, n4_to_16_decoder_w_enable_1__15;
  wire [15:0] R0_q, R1_q, R2_q, R3_q, R4_q, R5_q, R6_q, R7_q, R8_q, R9_q, R10_q, R11_q, R12_q, R13_q, R14_q,
       R15_q;

  _4_to_16_decoder_w__enable u_4_to_16_decoder_w_enable_1 (
    .Select(WriteAddress), .Enable(Write), ._1(n4_to_16_decoder_w_enable_1__1),
    ._2(n4_to_16_decoder_w_enable_1__2), ._3(n4_to_16_decoder_w_enable_1__3),
    ._4(n4_to_16_decoder_w_enable_1__4), ._5(n4_to_16_decoder_w_enable_1__5),
    ._6(n4_to_16_decoder_w_enable_1__6), ._7(n4_to_16_decoder_w_enable_1__7),
    ._8(n4_to_16_decoder_w_enable_1__8), ._9(n4_to_16_decoder_w_enable_1__9),
    ._10(n4_to_16_decoder_w_enable_1__10), ._11(n4_to_16_decoder_w_enable_1__11),
    ._12(n4_to_16_decoder_w_enable_1__12), ._13(n4_to_16_decoder_w_enable_1__13),
    ._14(n4_to_16_decoder_w_enable_1__14), ._15(n4_to_16_decoder_w_enable_1__15));  // open: _0
  Register #(.width(16), .trigger("rising")) R0 (.D(WriteData), .en(1'b0), .Q(R0_q), .clk(CLK), .clr(Clear));
  Register #(.width(16), .trigger("rising")) R4 (
    .D(WriteData), .en(n4_to_16_decoder_w_enable_1__4), .Q(R4_q), .clk(CLK), .clr(Clear));
  Register #(.width(16), .trigger("rising")) R8 (
    .D(WriteData), .en(n4_to_16_decoder_w_enable_1__8), .Q(R8_q), .clk(CLK), .clr(Clear));
  Register #(.width(16), .trigger("rising")) R12 (
    .D(WriteData), .en(n4_to_16_decoder_w_enable_1__12), .Q(R12_q), .clk(CLK), .clr(Clear));
  Register #(.width(16), .trigger("rising")) R1 (
    .D(WriteData), .en(n4_to_16_decoder_w_enable_1__1), .Q(R1_q), .clk(CLK), .clr(Clear));
  Register #(.width(16), .trigger("rising")) R5 (
    .D(WriteData), .en(n4_to_16_decoder_w_enable_1__5), .Q(R5_q), .clk(CLK), .clr(Clear));
  Register #(.width(16), .trigger("rising")) R9 (
    .D(WriteData), .en(n4_to_16_decoder_w_enable_1__9), .Q(R9_q), .clk(CLK), .clr(Clear));
  Register #(.width(16), .trigger("rising")) R13 (
    .D(WriteData), .en(n4_to_16_decoder_w_enable_1__13), .Q(R13_q), .clk(CLK), .clr(Clear));
  Register #(.width(16), .trigger("rising")) R2 (
    .D(WriteData), .en(n4_to_16_decoder_w_enable_1__2), .Q(R2_q), .clk(CLK), .clr(Clear));
  Register #(.width(16), .trigger("rising")) R6 (
    .D(WriteData), .en(n4_to_16_decoder_w_enable_1__6), .Q(R6_q), .clk(CLK), .clr(Clear));
  Register #(.width(16), .trigger("rising")) R10 (
    .D(WriteData), .en(n4_to_16_decoder_w_enable_1__10), .Q(R10_q), .clk(CLK), .clr(Clear));
  Register #(.width(16), .trigger("rising")) R14 (
    .D(WriteData), .en(n4_to_16_decoder_w_enable_1__14), .Q(R14_q), .clk(CLK), .clr(Clear));
  Register #(.width(16), .trigger("rising")) R3 (
    .D(WriteData), .en(n4_to_16_decoder_w_enable_1__3), .Q(R3_q), .clk(CLK), .clr(Clear));
  Register #(.width(16), .trigger("rising")) R7 (
    .D(WriteData), .en(n4_to_16_decoder_w_enable_1__7), .Q(R7_q), .clk(CLK), .clr(Clear));
  Register #(.width(16), .trigger("rising")) R11 (
    .D(WriteData), .en(n4_to_16_decoder_w_enable_1__11), .Q(R11_q), .clk(CLK), .clr(Clear));
  Register #(.width(16), .trigger("rising")) R15 (
    .D(WriteData), .en(n4_to_16_decoder_w_enable_1__15), .Q(R15_q), .clk(CLK), .clr(Clear));
  Multiplexer #(.select(4), .width(16)) multiplexer_1 (
    .in0(R0_q), .in1(R1_q), .in2(R2_q), .in3(R3_q), .in4(R4_q), .in5(R5_q), .in6(R6_q), .in7(R7_q),
    .in8(R8_q), .in9(R9_q), .in10(R10_q), .in11(R11_q), .in12(R12_q), .in13(R13_q), .in14(R14_q),
    .in15(R15_q), .out(Out1), .sel(ReadAddress1));
  Multiplexer #(.select(4), .width(16)) multiplexer_2 (
    .in0(R0_q), .in1(R1_q), .in2(R2_q), .in3(R3_q), .in4(R4_q), .in5(R5_q), .in6(R6_q), .in7(R7_q),
    .in8(R8_q), .in9(R9_q), .in10(R10_q), .in11(R11_q), .in12(R12_q), .in13(R13_q), .in14(R14_q),
    .in15(R15_q), .out(Out2), .sel(ReadAddress2));
  Multiplexer #(.select(4), .width(16)) multiplexer_3 (
    .in0(R0_q), .in1(R1_q), .in2(R2_q), .in3(R3_q), .in4(R4_q), .in5(R5_q), .in6(R6_q), .in7(R7_q),
    .in8(R8_q), .in9(R9_q), .in10(R10_q), .in11(R11_q), .in12(R12_q), .in13(R13_q), .in14(R14_q),
    .in15(R15_q), .out(Out3), .sel(ReadAddress3));
endmodule

module _4_to_16_decoder_w__enable (
  input  [3:0] Select,
  input  Enable,
  output _0,
  output _1,
  output _2,
  output _3,
  output _4,
  output _5,
  output _6,
  output _7,
  output _8,
  output _9,
  output _10,
  output _11,
  output _12,
  output _13,
  output _14,
  output _15
);

  wire not_1_out, not_2_out, not_3_out, not_4_out;

  not not_1 (not_1_out, Select[0]);
  not not_2 (not_2_out, Select[1]);
  not not_3 (not_3_out, Select[2]);
  not not_4 (not_4_out, Select[3]);
  and and_1 (_0, not_1_out, not_2_out, not_3_out, not_4_out, Enable);
  and and_2 (_1, Select[0], not_2_out, not_3_out, not_4_out, Enable);
  and and_3 (_2, not_1_out, Select[1], not_3_out, not_4_out, Enable);
  and and_4 (_3, Select[0], Select[1], not_3_out, not_4_out, Enable);
  and and_5 (_4, not_1_out, not_2_out, Select[2], not_4_out, Enable);
  and and_6 (_5, Select[0], not_2_out, Select[2], not_4_out, Enable);
  and and_7 (_6, not_1_out, Select[1], not_4_out, Select[2], Enable);
  and and_8 (_7, Select[0], Select[1], Select[2], not_4_out, Enable);
  and and_9 (_8, Select[3], Enable, not_3_out, not_2_out, not_1_out);
  and and_10 (_9, not_2_out, not_3_out, Select[0], Select[3], Enable);
  and and_11 (_10, not_1_out, not_3_out, Select[1], Select[3], Enable);
  and and_12 (_11, not_3_out, Select[0], Select[1], Select[3], Enable);
  and and_13 (_12, not_1_out, not_2_out, Select[2], Select[3], Enable);
  and and_14 (_13, not_2_out, Select[0], Select[2], Select[3], Enable);
  and and_15 (_14, not_1_out, Select[1], Select[2], Select[3], Enable);
  and and_16 (_15, Select[3], Select[2], Select[1], Select[0], Enable);

  // Notes on the sheet:
  //   0
  //   1
  //   2
  //   3
endmodule

module _4_bit_sign_extend (
  input  [3:0] in,
  output [15:0] out
);


  assign out = {{13{in[3]}}, in[2:0]};
endmodule

module _8_bit_sign_extend (
  input  [7:0] in,
  output [15:0] out
);


  assign out = {{9{in[7]}}, in[6:0]};
endmodule

module data_path (
  input  PCsrc,
  input  RegWrite,
  input  A_S,
  input  [2:0] ALUop,
  input  RegData,
  input  BorImmS,
  input  CLK,
  input  Clear,
  output [3:0] opcode,
  output z_e_r_o
);

  wire [11:0] rom_1_data;
  wire [15:0] adder_1_out, adder_2_out, multiplexer_1_out, multiplexer_2_out, multiplexer_3_out,
       n4_bit_sign_extend_1_out, n8_bit_sign_extend_1_out, n16_bit_alu_1_result, PC_q, reg_file_1_out1,
       reg_file_1_out2, reg_file_1_out3;

  Multiplexer #(.select(1), .width(16)) multiplexer_1 (
    .in0(adder_1_out), .in1(adder_2_out), .out(multiplexer_1_out), .sel(PCsrc));
  Register #(.width(16), .trigger("rising")) PC (.D(multiplexer_1_out), .en(1'b1), .Q(PC_q), .clk(CLK), .clr(Clear));
  Adder #(.width(16)) adder_1 (.a(16'h1), .b(PC_q), .out(adder_1_out));  // open: cin, cout
  ROM #(.addrWidth(16), .dataWidth(16)) rom_1 (.addr(PC_q), .data({opcode, rom_1_data}));  // open: sel
  _4_bit_sign_extend u_4_bit_sign_extend_1 (.in(rom_1_data[3:0]), .out(n4_bit_sign_extend_1_out));
  _8_bit_sign_extend u_8_bit_sign_extend_1 (.in(rom_1_data[7:0]), .out(n8_bit_sign_extend_1_out));
  reg_file reg_file_1 (
    .ReadAddress1(rom_1_data[7:4]), .ReadAddress2(rom_1_data[3:0]), .ReadAddress3(rom_1_data[11:8]),
    .WriteAddress(rom_1_data[11:8]), .Write(RegWrite), .WriteData(multiplexer_3_out), .CLK(CLK),
    .Clear(Clear), .Out1(reg_file_1_out1), .Out2(reg_file_1_out2), .Out3(reg_file_1_out3));
  Multiplexer #(.select(1), .width(16)) multiplexer_2 (
    .in0(reg_file_1_out2), .in1(n4_bit_sign_extend_1_out), .out(multiplexer_2_out), .sel(BorImmS));
  Adder #(.width(16)) adder_2 (.a(PC_q), .b(reg_file_1_out3), .out(adder_2_out));  // open: cin, cout
  _16_bit_alu u_16_bit_alu_1 (
    .A(reg_file_1_out1), .B(multiplexer_2_out), .Add_Sub(A_S), .Select(ALUop), .z_e_r_o(z_e_r_o),
    .Result(n16_bit_alu_1_result));  // open: Overflow
  Multiplexer #(.select(1), .width(16)) multiplexer_3 (
    .in0(n16_bit_alu_1_result), .in1(n8_bit_sign_extend_1_out), .out(multiplexer_3_out), .sel(RegData));

  // Notes on the sheet:
  //   contents of rom_1 (hex, n*v repeats v):
  //   c106 c303 c4fe d321 a221 f400
  //   Regs
  //   4 SE
  //   8 SE
  //   ALU
endmodule

module control_unit (
  input  z_e_r_o,
  input  [3:0] opcode,
  output PCsrc,
  output RegWrite,
  output BorImmS,
  output A_S,
  output RegData,
  output [2:0] ALUop
);

  wire and_1_out, and_2_out, decoder_1_out0, decoder_1_out1, decoder_1_out2, decoder_1_out3, decoder_1_out4,
       decoder_1_out5, decoder_1_out6, decoder_1_out7, decoder_1_out8, decoder_1_out9, decoder_1_out10,
       decoder_1_out11, decoder_1_out13, decoder_1_out14, decoder_1_out15, not_1_out;

  Decoder #(.select(4), .tristate("false")) decoder_1 (
    .out0(decoder_1_out0), .out1(decoder_1_out1), .out2(decoder_1_out2), .out3(decoder_1_out3),
    .out4(decoder_1_out4), .out5(decoder_1_out5), .out6(decoder_1_out6), .out7(decoder_1_out7),
    .out8(decoder_1_out8), .out9(decoder_1_out9), .out10(decoder_1_out10), .out11(decoder_1_out11),
    .out12(RegData), .out13(decoder_1_out13), .out14(decoder_1_out14), .out15(decoder_1_out15), .sel(opcode));
  or or_1 (BorImmS, decoder_1_out11, decoder_1_out10, decoder_1_out9, decoder_1_out8);
  not not_1 (not_1_out, z_e_r_o);
  nor nor_1 (RegWrite, decoder_1_out15, decoder_1_out14, decoder_1_out13);
  or or_2 (A_S, decoder_1_out3, decoder_1_out4, decoder_1_out11, decoder_1_out13, decoder_1_out14);
  and and_1 (and_1_out, not_1_out, decoder_1_out14);
  and and_2 (and_2_out, z_e_r_o, decoder_1_out13);
  or or_3 (PCsrc, decoder_1_out15, and_1_out, and_2_out);
  or or_4 (ALUop[2], decoder_1_out5, decoder_1_out6, decoder_1_out7);
  or or_5 (ALUop[1], A_S, decoder_1_out2, decoder_1_out10, decoder_1_out7);
  or or_6 (ALUop[0], decoder_1_out1, decoder_1_out9, decoder_1_out4, decoder_1_out11, decoder_1_out6);

  // Notes on the sheet:
  //   and
  //   or
  //   add
  //   sub
  //   not
  //   lshft
  //   slt
  //   andi
  //   rshft
  //   ori
  //   addi
  //   slti
  //   beq
  //   li
  //   j
  //   bne
  //   I-Type
  //   !CEL
endmodule

module full_cpu (
);

  wire button_1_out, button_2_out, control_unit_1_a_s, control_unit_1_borimms, control_unit_1_pcsrc,
       control_unit_1_regdata, control_unit_1_regwrite, data_path_1_z_e_r_o;
  wire [2:0] control_unit_1_aluop;
  wire [3:0] data_path_1_opcode;

  control_unit control_unit_1 (
    .z_e_r_o(data_path_1_z_e_r_o), .opcode(data_path_1_opcode), .PCsrc(control_unit_1_pcsrc),
    .RegWrite(control_unit_1_regwrite), .BorImmS(control_unit_1_borimms), .A_S(control_unit_1_a_s),
    .RegData(control_unit_1_regdata), .ALUop(control_unit_1_aluop));
  data_path data_path_1 (
    .opcode(data_path_1_opcode), .z_e_r_o(data_path_1_z_e_r_o), .CLK(button_1_out), .Clear(button_2_out),
    .PCsrc(control_unit_1_pcsrc), .RegWrite(control_unit_1_regwrite), .A_S(control_unit_1_a_s),
    .ALUop(control_unit_1_aluop), .RegData(control_unit_1_regdata), .BorImmS(control_unit_1_borimms));
  Button button_1 (.out(button_1_out));
  Button button_2 (.out(button_2_out));
  Clock #(.highDuration(1), .lowDuration(1)) clock_1 ();  // open: out

  // Notes on the sheet:
  //   CU
  //   DP
  //   CLR
  //   CLK
endmodule
